# Fritzing sketch Breadboard v1 (saved by Fritzing 0.9.0b)
breadboards: 1

parts:
  ESC = mystery part, 3 pins [chip_label=? spacing=300mil]
  R3 = Resistor [tolerance=±5% resistance=220 package=THT]
  R4 = Resistor [tolerance=±5% resistance=6.8k package=THT]
  J1 = female pin header, 2 pins [form="♀ (female)"]
  J2 = female pin header, 2 pins [form="♀ (female)"]
  Lock = Pushbutton [package=THT]
  Stop = Pushbutton [package=THT]
  Start = Pushbutton [package=THT]
  Short = Pushbutton [package=THT]
  R5 = Resistor [tolerance=±5% resistance=2.2k package=THT]
  R6 = Resistor [tolerance=±5% resistance=2.2k package=THT]
  R7 = Resistor [tolerance=±5% resistance=2.2k package=THT]
  R8 = Resistor [tolerance=±5% resistance=2.2k package=THT]
  Arduino1 = Arduino Uno (Rev3)
  RE1 = Rotary Encoder [package=THT]
  RE2 = Rotary Encoder [package=THT]
  LCD1 = LCD screen

nets (from the breadboard view):
  GND: ESC.pin1, J1.pin1, J2.pin1, Short.leg0, R6.Pin_0, R7.Pin_0, R8.Pin_0, Arduino1.GND, RE1.EncoderPinC, RE2.EncoderPinC, LCD1.VSS
  N1: ESC.pin3, Stop.leg1, R7.Pin_1, Arduino1.D7
  3V3: R3.Pin_0, R4.Pin_0, Lock.leg0, Stop.leg0, Start.leg0, R5.Pin_0, Arduino1.3V3, LCD1.VDD
  N2: R3.Pin_1, J2.pin2
  N3: R4.Pin_1, J1.pin2, Arduino1.D2
  N4: Lock.leg1, R8.Pin_1, Arduino1.D6_PWM
  N5: Start.leg1, R5.Pin_1, R6.Pin_1, Arduino1.D4
  N6: Arduino1.A0, RE2.EncoderPinA
  N7: Arduino1.A1, RE2.EncoderPinB
  N8: Arduino1.A4/SDA, LCD1.V0
  N9: Arduino1.A5/SCL, LCD1.RS
  N10: Arduino1.D8, RE1.EncoderPinB
  N11: Arduino1.D9_PWM, RE1.EncoderPinA

notes:
  IR sensor
