# Fritzing sketch Shield v1.0 (saved by Fritzing 0.9.0b)

parts:
  ESC3 = mystery part, 3 pins [chip_label=? spacing=300mil]
  Onderdeel3 = Arduino Prototyping Shield
  LCD3 = LCD screen
  RE6 = Rotary Encoder [package=THT]
  S5 = Pushbutton [package=THT]
  S6 = Pushbutton [package=THT]
  S7 = Pushbutton [package=THT]
  S8 = Pushbutton [package=THT]
  R15 = Resistor [tolerance=±5% resistance=2.2k package=THT]
  R16 = Resistor [tolerance=±5% resistance=2.2k package=THT]
  R17 = Resistor [tolerance=±5% resistance=2.2k package=THT]
  R18 = Resistor [tolerance=±5% resistance=2.2k package=THT]
  RE7 = Rotary Encoder [package=THT]
  J9 = female pin header, 8 pins [form="♀ (female)"]
  J10 = female pin header, 8 pins [form="♀ (female)"]
  J11 = female pin header, 1 pin [form="♀ (female)"]
  J12 = female pin header, 6 pins [form="♀ (female)"]  # not connected
  J13 = female pin header, 6 pins [form="♀ (female)"]
  R19 = Resistor [tolerance=±5% resistance=220 package=THT]
  R20 = Resistor [tolerance=±5% resistance=6.8k package=THT]
  IR1 = mystery part, 4 pins [chip_label=?]

nets:
  GND: ESC3.pin1, Onderdeel3.GND, LCD3.VSS, RE6.EncoderPinC, S5.leg0, S6.leg0, S7.leg0, S8.leg0, RE7.EncoderPinC, J10.pin6, J10.pin7, IR1.pin2, IR1.pin4
  N1: ESC3.pin3, Onderdeel3.D7, J9.pin1
  N2: Onderdeel3.A0, RE7.EncoderPinB, J13.pin1
  N3: Onderdeel3.A1, RE7.EncoderPinA, J13.pin2
  N4: Onderdeel3.A2, J13.pin3
  N5: Onderdeel3.A3, J13.pin4
  N6: Onderdeel3.A4, LCD3.V0, J13.pin5
  N7: Onderdeel3.A5, LCD3.RS, J13.pin6
  N8: Onderdeel3.D0(RX), J9.pin8
  N9: Onderdeel3.D1(TX), J9.pin7
  N10: Onderdeel3.D2, J9.pin6, R20.Pin_1, IR1.pin1
  N11: Onderdeel3.D3, S8.leg1, R16.Pin_1, J9.pin5
  N12: Onderdeel3.D4, S6.leg1, R17.Pin_1, J9.pin4
  N13: Onderdeel3.D5, S7.leg1, R18.Pin_1, J9.pin3
  N14: Onderdeel3.D6, S5.leg1, R15.Pin_1, J9.pin2
  N15: Onderdeel3.IOREF, J10.pin1, J10.pin2
  N16: Onderdeel3.RESET, J10.pin3
  N17: Onderdeel3.3.3V, J10.pin4
  +5V: Onderdeel3.+5V, Onderdeel3.N$405, Onderdeel3.N$407, Onderdeel3.N$409, Onderdeel3.N$412, Onderdeel3.N$413, LCD3.VDD, R15.Pin_0, R16.Pin_0, R17.Pin_0, R18.Pin_0, J10.pin5, R19.Pin_1
  N18: Onderdeel3.+9V, J10.pin8
  N19: Onderdeel3.D8, RE6.EncoderPinB
  N20: Onderdeel3.D9, RE6.EncoderPinA
  N21: Onderdeel3.N$117, J11.pin1, IR1.pin3
  N22: Onderdeel3.N$393, R19.Pin_0
  N23: Onderdeel3.N$406, R20.Pin_0
